// Logisim project Adders_Logisim.circ as structural Verilog
module FULL_ADDER (
  input  A,
  input  B,
  input  C_in,
  output S,
  output C_out
);

  wire and_1_out, and_2_out, xor_1_out;

  xor xor_1 (xor_1_out, A, B);
  xor xor_2 (S, xor_1_out, C_in);
  and and_1 (and_1_out, xor_1_out, C_in);
  and and_2 (and_2_out, A, B);
  or or_1 (C_out, and_1_out, and_2_out);
endmodule

module RIPPLE_CARRY (
  input  A0,
  input  B0,
  input  C_in,
  input  A1,
  input  B1,
  input  A2,
  input  B2,
  input  A3,
  input  B3
);

  wire C_out0, C_out1, C_out2, full_adder_1_s, full_adder_2_s, full_adder_3_s, full_adder_4_c_out,
       full_adder_4_s;

  FULL_ADDER full_adder_1 (.A(A0), .B(B0), .C_in(C_in), .S(full_adder_1_s), .C_out(C_out0));
  FULL_ADDER full_adder_2 (.A(A1), .B(B1), .C_in(C_out0), .S(full_adder_2_s), .C_out(C_out1));
  FULL_ADDER full_adder_3 (.A(A2), .B(B2), .C_in(C_out1), .S(full_adder_3_s), .C_out(C_out2));
  FULL_ADDER full_adder_4 (.A(A3), .B(B3), .C_in(C_out2), .S(full_adder_4_s), .C_out(full_adder_4_c_out));
  // Probe on full_adder_1_s
  // Probe on full_adder_2_s
  // Probe on full_adder_3_s
  // Probe on full_adder_4_s
  // Probe on full_adder_4_c_out
endmodule

module CARRY_LOOKAHEAD (
  input  A3,
  input  B3,
  input  A2,
  input  B2,
  input  A1,
  input  B1,
  input  in_7,
  input  A0,
  input  B0,
  output C4,
  output S3,
  output S2,
  output S1,
  output S0
);

  wire carry_lookahead_block2_1_c0, carry_lookahead_block2_1_c1, carry_lookahead_block2_1_c2,
       carry_lookahead_block2_1_c3, carry_lookahead_block2_1_p_0, carry_lookahead_block2_1_p_1,
       carry_lookahead_block2_1_p_2, carry_lookahead_block2_1_p_3, p_and_g_1_g, p_and_g_1_p, p_and_g_2_g,
       p_and_g_2_p, p_and_g_3_g, p_and_g_3_p, p_and_g_4_g, p_and_g_4_p;

  P_AND_G p_and_g_1 (.A(A3), .B(B3), .P(p_and_g_1_p), .G(p_and_g_1_g));
  P_AND_G p_and_g_2 (.A(A2), .B(B2), .P(p_and_g_2_p), .G(p_and_g_2_g));
  P_AND_G p_and_g_3 (.A(A1), .B(B1), .P(p_and_g_3_p), .G(p_and_g_3_g));
  P_AND_G p_and_g_4 (.A(A0), .B(B0), .P(p_and_g_4_p), .G(p_and_g_4_g));
  CARRY_LOOKAHEAD_BLOCK2 carry_lookahead_block2_1 (
    .P3(p_and_g_1_p), .G3(p_and_g_1_g), .P2(p_and_g_2_p), .G2(p_and_g_2_g), .P1(p_and_g_3_p),
    .G1(p_and_g_3_g), .P0(p_and_g_4_p), .G0(p_and_g_4_g), .C_in(in_7), .C4(C4),
    .C3(carry_lookahead_block2_1_c3), .P_3(carry_lookahead_block2_1_p_3), .C2(carry_lookahead_block2_1_c2),
    .P_2(carry_lookahead_block2_1_p_2), .C1(carry_lookahead_block2_1_c1), .P_1(carry_lookahead_block2_1_p_1),
    .P_0(carry_lookahead_block2_1_p_0), .C0(carry_lookahead_block2_1_c0));
  xor xor_1 (S3, carry_lookahead_block2_1_c3, carry_lookahead_block2_1_p_3);
  xor xor_2 (S2, carry_lookahead_block2_1_c2, carry_lookahead_block2_1_p_2);
  xor xor_3 (S1, carry_lookahead_block2_1_c1, carry_lookahead_block2_1_p_1);
  xor xor_4 (S0, carry_lookahead_block2_1_p_0, carry_lookahead_block2_1_c0);
endmodule

module P_AND_G (
  input  A,
  input  B,
  output P,
  output G
);

  xor xor_1 (P, A, B);
  and and_1 (G, A, B);
endmodule

module Prefix_Block (
  input  [3:0] P,
  input  [3:0] G,
  input  C_in,
  output [3:0] G_out,
  output C_out
);

  wire and_1_out, and_2_out, and_3_out, and_4_out, and_5_out, and_6_out, or_2_out;

  and and_1 (and_1_out, C_in, P[0]);
  and and_2 (and_2_out, G[1], P[2]);
  and and_3 (and_3_out, P[1], P[2]);
  or or_1 (G_out[1], and_1_out, G[0]);
  or or_2 (or_2_out, and_2_out, G[2]);
  and and_4 (and_4_out, G_out[1], P[1]);
  and and_5 (and_5_out, G_out[1], and_3_out);
  or or_3 (G_out[3], and_5_out, or_2_out);
  or or_4 (G_out[2], and_4_out, G[1]);
  and and_6 (and_6_out, G_out[3], P[3]);
  or or_5 (C_out, and_6_out, G[3]);

  assign G_out[0] = C_in;
endmodule

module GenerateP_G (
  input  [3:0] A,
  input  [3:0] B,
  output [3:0] P,
  output [3:0] G
);

  or or_1 (P[0], A[0], B[0]);
  and and_1 (G[0], A[0], B[0]);
  or or_2 (P[1], A[1], B[1]);
  and and_2 (G[1], A[1], B[1]);
  or or_3 (P[2], A[2], B[2]);
  and and_3 (G[2], A[2], B[2]);
  or or_4 (P[3], A[3], B[3]);
  and and_4 (G[3], A[3], B[3]);
endmodule

module Prefix_Logic (
  input  [3:0] A,
  input  [3:0] B,
  input  in_3,
  output [3:0] S,
  output C_out
);

  wire [3:0] generatep_g_1_g, generatep_g_1_p, prefix_block_1_g_out;

  GenerateP_G generatep_g_1 (.A(A), .B(B), .P(generatep_g_1_p), .G(generatep_g_1_g));
  Prefix_Block prefix_block_1 (
    .P(generatep_g_1_p), .G(generatep_g_1_g), .C_in(in_3), .G_out(prefix_block_1_g_out), .C_out(C_out));
  Prefix_ADDER prefix_adder_1 (.A(A), .B(B), .G_out(prefix_block_1_g_out), .S(S));
endmodule

module Prefix_ADDER (
  input  [3:0] A,
  input  [3:0] B,
  input  [3:0] G_out,
  output [3:0] S
);

  wire xor_1_out, xor_2_out, xor_3_out, xor_4_out;

  xor xor_1 (xor_1_out, A[0], B[0]);
  xor xor_2 (xor_2_out, A[1], B[1]);
  xor xor_3 (xor_3_out, A[2], B[2]);
  xor xor_4 (xor_4_out, A[3], B[3]);
  xor xor_5 (S[0], xor_1_out, G_out[0]);
  xor xor_6 (S[1], xor_2_out, G_out[1]);
  xor xor_7 (S[2], xor_3_out, G_out[2]);
  xor xor_8 (S[3], xor_4_out, G_out[3]);
endmodule

module CARRY_LOOKAHEAD_BLOCK2 (
  input  P3,
  input  G3,
  input  P2,
  input  G2,
  input  P1,
  input  G1,
  input  P0,
  input  G0,
  input  C_in,
  output C4,
  output C3,
  output P_3,
  output C2,
  output P_2,
  output C1,
  output P_1,
  output P_0,
  output C0
);

  wire and_1_out, and_2_out, and_3_out, and_4_out, and_5_out, and_6_out, and_7_out, and_8_out, and_9_out,
       and_10_out, and_11_out, and_12_out, and_13_out, and_14_out, and_15_out, and_16_out, and_17_out,
       and_18_out, and_19_out, and_20_out, or_1_out, or_2_out, or_3_out, or_4_out, or_5_out, or_6_out;

  and and_1 (and_1_out, G0, P1);
  and and_2 (and_2_out, G1, P2);
  and and_3 (and_3_out, P1, P0);
  and and_4 (and_4_out, P1, G0);
  and and_5 (and_5_out, P0, C_in);
  and and_6 (and_6_out, C_in, P0);
  and and_7 (and_7_out, P1, P2);
  and and_8 (and_8_out, G0, P1);
  and and_9 (and_9_out, P2, P3);
  and and_10 (and_10_out, G1, P2);
  and and_11 (and_11_out, G2, P3);
  and and_12 (and_12_out, C_in, P0);
  and and_13 (and_13_out, P1, P2);
  and and_14 (and_14_out, and_6_out, and_7_out);
  and and_15 (and_15_out, and_8_out, and_9_out);
  and and_16 (and_16_out, and_10_out, P3);
  and and_17 (and_17_out, and_12_out, and_13_out);
  and and_18 (and_18_out, and_1_out, P2);
  and and_19 (and_19_out, and_3_out, C_in);
  and and_20 (and_20_out, and_14_out, P3);
  or or_1 (or_1_out, and_20_out, and_15_out);
  or or_2 (or_2_out, and_16_out, and_11_out);
  or or_3 (or_3_out, and_17_out, and_18_out);
  or or_4 (or_4_out, and_2_out, G2);
  or or_5 (or_5_out, and_19_out, and_4_out);
  or or_6 (or_6_out, or_1_out, or_2_out);
  or or_7 (C3, or_3_out, or_4_out);
  or or_8 (C2, or_5_out, G1);
  or or_9 (C1, and_5_out, G0);
  or or_10 (C4, or_6_out, G3);

  assign C0 = C_in;
  assign P_0 = P0;
  assign P_1 = P1;
  assign P_2 = P2;
  assign P_3 = P3;
endmodule
