// Logisim project ALU_Diego_Lemus.circ as structural Verilog
module Prefix_Block (
  input  [3:0] P,
  input  [3:0] G,
  input  C_in,
  output [3:0] G_out,
  output C_out
);

  wire and_1_out, and_2_out, and_3_out, and_4_out, and_5_out, and_6_out, or_2_out;

  and and_1 (and_1_out, C_in, P[0]);
  and and_2 (and_2_out, G[1], P[2]);
  and and_3 (and_3_out, P[1], P[2]);
  or or_1 (G_out[1], and_1_out, G[0]);
  or or_2 (or_2_out, and_2_out, G[2]);
  and and_4 (and_4_out, G_out[1], P[1]);
  and and_5 (and_5_out, G_out[1], and_3_out);
  or or_3 (G_out[3], and_5_out, or_2_out);
  or or_4 (G_out[2], and_4_out, G[1]);
  and and_6 (and_6_out, G_out[3], P[3]);
  or or_5 (C_out, and_6_out, G[3]);

  assign G_out[0] = C_in;
endmodule

module GenerateP_G (
  input  [3:0] A,
  input  [3:0] B,
  output [3:0] P,
  output [3:0] G
);

  or or_1 (P[0], A[0], B[0]);
  and and_1 (G[0], A[0], B[0]);
  or or_2 (P[1], A[1], B[1]);
  and and_2 (G[1], A[1], B[1]);
  or or_3 (P[2], A[2], B[2]);
  and and_3 (G[2], A[2], B[2]);
  or or_4 (P[3], A[3], B[3]);
  and and_4 (G[3], A[3], B[3]);
endmodule

module Prefix_Logic (
  input  [3:0] A,
  input  [3:0] B,
  input  C_in,
  output [3:0] S,
  output C_out
);

  wire [3:0] generatep_g_1_g, generatep_g_1_p, prefix_block_1_g_out;

  GenerateP_G generatep_g_1 (.A(A), .B(B), .P(generatep_g_1_p), .G(generatep_g_1_g));
  Prefix_Block prefix_block_1 (
    .P(generatep_g_1_p), .G(generatep_g_1_g), .C_in(C_in), .G_out(prefix_block_1_g_out), .C_out(C_out));
  Prefix_ADDER prefix_adder_1 (.A(A), .B(B), .G_out(prefix_block_1_g_out), .S(S));
endmodule

module Prefix_ADDER (
  input  [3:0] A,
  input  [3:0] B,
  input  [3:0] G_out,
  output [3:0] S
);

  wire xor_1_out, xor_2_out, xor_3_out, xor_4_out;

  xor xor_1 (xor_1_out, A[0], B[0]);
  xor xor_2 (xor_2_out, A[1], B[1]);
  xor xor_3 (xor_3_out, A[2], B[2]);
  xor xor_4 (xor_4_out, A[3], B[3]);
  xor xor_5 (S[0], xor_1_out, G_out[0]);
  xor xor_6 (S[1], xor_2_out, G_out[1]);
  xor xor_7 (S[2], xor_3_out, G_out[2]);
  xor xor_8 (S[3], xor_4_out, G_out[3]);
endmodule

module ShiftRight (
  input  [1:0] SHIFTRIGHT,
  input  [3:0] SUMREST,
  output [3:0] out_3
);

  Multiplexer #(.select(2)) multiplexer_1 (
    .in0(SUMREST[0]), .in1(1'b0), .in2(1'b0), .in3(1'b0), .out(out_3[3]), .sel(SHIFTRIGHT));
  Multiplexer #(.select(2)) multiplexer_2 (
    .in0(SUMREST[0]), .in1(SUMREST[1]), .in2(1'b0), .in3(1'b0), .out(out_3[2]), .sel(SHIFTRIGHT));
  Multiplexer #(.select(2)) multiplexer_3 (
    .in0(SUMREST[2]), .in1(SUMREST[1]), .in2(SUMREST[0]), .in3(1'b0), .out(out_3[1]), .sel(SHIFTRIGHT));
  Multiplexer #(.select(2)) multiplexer_4 (
    .in0(SUMREST[3]), .in1(SUMREST[2]), .in2(SUMREST[1]), .in3(SUMREST[0]), .out(out_3[0]), .sel(SHIFTRIGHT));
endmodule

module ShiftLeft (
  input  [1:0] SHIFT_LEFT,
  input  [3:0] SUMARESTA,
  output [3:0] out_3
);

  Multiplexer #(.select(2)) multiplexer_1 (
    .in0(SUMARESTA[0]), .in1(SUMARESTA[1]), .in2(SUMARESTA[2]), .in3(SUMARESTA[3]), .out(out_3[3]),
    .sel(SHIFT_LEFT));
  Multiplexer #(.select(2)) multiplexer_2 (
    .in0(SUMARESTA[2]), .in1(SUMARESTA[1]), .in2(SUMARESTA[0]), .in3(1'b0), .out(out_3[2]), .sel(SHIFT_LEFT));
  Multiplexer #(.select(2)) multiplexer_3 (
    .in0(SUMARESTA[1]), .in1(SUMARESTA[0]), .in2(1'b0), .in3(1'b0), .out(out_3[1]), .sel(SHIFT_LEFT));
  Multiplexer #(.select(2)) multiplexer_4 (
    .in0(SUMARESTA[0]), .in1(1'b0), .in2(1'b0), .in3(1'b0), .out(out_3[0]), .sel(SHIFT_LEFT));
endmodule

module SumRest (
  input  ALU0,
  input  [3:0] A,
  input  [3:0] B,
  output [3:0] SumResta,
  output C_out
);

  wire [3:0] multiplexer_1_out, not_1_out;

  assign not_1_out = ~B;  // NOT_Gate not_1, 4 bits wide
  Multiplexer #(.width(4)) multiplexer_1 (.in0(B), .in1(not_1_out), .out(multiplexer_1_out), .sel(ALU0));
  Prefix_Logic prefix_logic_1 (.A(A), .B(multiplexer_1_out), .C_in(ALU0), .S(SumResta), .C_out(C_out));
endmodule

module ORR (
  input  [3:0] A,
  input  [3:0] B,
  output [3:0] out_3
);

  or or_1 (out_3[0], A[0], B[0]);
  or or_2 (out_3[1], A[1], B[1]);
  or or_3 (out_3[2], A[2], B[2]);
  or or_4 (out_3[3], A[3], B[3]);
endmodule

module ANDD (
  input  [3:0] A,
  input  [3:0] B,
  output [3:0] out_3
);

  and and_1 (out_3[0], A[0], B[0]);
  and and_2 (out_3[1], A[1], B[1]);
  and and_3 (out_3[2], A[2], B[2]);
  and and_4 (out_3[3], A[3], B[3]);
endmodule
