// Logisim project ALU_Diego_Lemus.circ as structural Verilog: 14 circuits, main circuit main
module main (
  input  [3:0] A,
  input  [3:0] B,
  input  [1:0] OP_Selector,
  input  [1:0] Shift_Selector,
  input  [1:0] Shift_Right,
  input  [1:0] Shift_Left,
  output [3:0] out_7,
  output [3:0] out_8
);

  wire alu_1_c_out, alu_1_cero, alu_1_negativo, alu_1_overflow;

  ALU alu_1 (
    .A(A), .B(B), .OP(OP_Selector), .OP_S(Shift_Selector), .SHIFT_R(Shift_Right), .SHIFT_L(Shift_Left),
    .Resultado(out_7), .A_Shift(out_8), .Cero(alu_1_cero), .Negativo(alu_1_negativo), .C_out(alu_1_c_out),
    .Overflow(alu_1_overflow));
  LED led_1 (.in(alu_1_cero));
  LED led_2 (.in(alu_1_negativo));
  LED led_3 (.in(alu_1_c_out));
  LED led_4 (.in(alu_1_overflow));
endmodule

module Prefix_Block (
  input  [3:0] P,
  input  [3:0] G,
  input  C_in,
  output [3:0] G_out,
  output C_out
);

  wire and_1_out, and_2_out, and_3_out, and_4_out, and_5_out, and_6_out, or_2_out;

  and and_1 (and_1_out, C_in, P[0]);
  and and_2 (and_2_out, G[1], P[2]);
  and and_3 (and_3_out, P[1], P[2]);
  or or_1 (G_out[1], and_1_out, G[0]);
  or or_2 (or_2_out, and_2_out, G[2]);
  and and_4 (and_4_out, G_out[1], P[1]);
  and and_5 (and_5_out, G_out[1], and_3_out);
  or or_3 (G_out[3], and_5_out, or_2_out);
  or or_4 (G_out[2], and_4_out, G[1]);
  and and_6 (and_6_out, G_out[3], P[3]);
  or or_5 (C_out, and_6_out, G[3]);

  assign G_out[0] = C_in;
endmodule

module GenerateP_G (
  input  [3:0] A,
  input  [3:0] B,
  output [3:0] P,
  output [3:0] G
);

  or or_1 (P[0], A[0], B[0]);
  and and_1 (G[0], A[0], B[0]);
  or or_2 (P[1], A[1], B[1]);
  and and_2 (G[1], A[1], B[1]);
  or or_3 (P[2], A[2], B[2]);
  and and_3 (G[2], A[2], B[2]);
  or or_4 (P[3], A[3], B[3]);
  and and_4 (G[3], A[3], B[3]);
endmodule

module Prefix_Logic (
  input  [3:0] A,
  input  [3:0] B,
  input  C_in,
  output [3:0] S,
  output C_out,
  output C2_Out,
  output C3_out
);

  wire [1:0] prefix_block_1_g_out;
  wire [3:0] generatep_g_1_g, generatep_g_1_p;

  GenerateP_G generatep_g_1 (.A(A), .B(B), .P(generatep_g_1_p), .G(generatep_g_1_g));
  Prefix_Block prefix_block_1 (
    .P(generatep_g_1_p), .G(generatep_g_1_g), .C_in(C_in), .G_out({C3_out, C2_Out, prefix_block_1_g_out}),
    .C_out(C_out));
  Prefix_ADDER prefix_adder_1 (.A(A), .B(B), .G_out({C3_out, C2_Out, prefix_block_1_g_out}), .S(S));
endmodule

module Prefix_ADDER (
  input  [3:0] A,
  input  [3:0] B,
  input  [3:0] G_out,
  output [3:0] S
);

  wire xor_1_out, xor_2_out, xor_3_out, xor_4_out;

  xor xor_1 (xor_1_out, A[0], B[0]);
  xor xor_2 (xor_2_out, A[1], B[1]);
  xor xor_3 (xor_3_out, A[2], B[2]);
  xor xor_4 (xor_4_out, A[3], B[3]);
  xor xor_5 (S[0], xor_1_out, G_out[0]);
  xor xor_6 (S[1], xor_2_out, G_out[1]);
  xor xor_7 (S[2], xor_3_out, G_out[2]);
  xor xor_8 (S[3], xor_4_out, G_out[3]);
endmodule

module ShiftRight (
  input  [1:0] SHIFTRIGHT,
  input  [3:0] A,
  output [3:0] out_3
);

  Multiplexer #(.select(2)) multiplexer_1 (
    .in0(A[3]), .in1(1'b0), .in2(1'b0), .in3(1'b0), .out(out_3[3]), .sel(SHIFTRIGHT));
  Multiplexer #(.select(2)) multiplexer_2 (
    .in0(A[2]), .in1(A[3]), .in2(1'b0), .in3(1'b0), .out(out_3[2]), .sel(SHIFTRIGHT));
  Multiplexer #(.select(2)) multiplexer_3 (
    .in0(A[1]), .in1(A[2]), .in2(A[3]), .in3(1'b0), .out(out_3[1]), .sel(SHIFTRIGHT));
  Multiplexer #(.select(2)) multiplexer_4 (
    .in0(A[0]), .in1(A[1]), .in2(A[2]), .in3(A[3]), .out(out_3[0]), .sel(SHIFTRIGHT));
endmodule

module ShiftLeft (
  input  [1:0] SHIFT_LEFT,
  input  [3:0] A,
  output [3:0] out_3
);

  Multiplexer #(.select(2)) multiplexer_1 (
    .in0(A[3]), .in1(A[2]), .in2(A[1]), .in3(A[0]), .out(out_3[3]), .sel(SHIFT_LEFT));
  Multiplexer #(.select(2)) multiplexer_2 (
    .in0(A[2]), .in1(A[1]), .in2(A[0]), .in3(1'b0), .out(out_3[2]), .sel(SHIFT_LEFT));
  Multiplexer #(.select(2)) multiplexer_3 (
    .in0(A[1]), .in1(A[0]), .in2(1'b0), .in3(1'b0), .out(out_3[1]), .sel(SHIFT_LEFT));
  Multiplexer #(.select(2)) multiplexer_4 (
    .in0(A[0]), .in1(1'b0), .in2(1'b0), .in3(1'b0), .out(out_3[0]), .sel(SHIFT_LEFT));
endmodule

module SumRest (
  input  Resta,
  input  [3:0] A,
  input  [3:0] B,
  output [3:0] SumResta,
  output C_out,
  output C2,
  output C3
);

  wire [3:0] multiplexer_1_out, not_1_out;

  assign not_1_out = ~B;  // NOT_Gate not_1, 4 bits wide
  Multiplexer #(.width(4)) multiplexer_1 (.in0(B), .in1(not_1_out), .out(multiplexer_1_out), .sel(Resta));
  Prefix_Logic prefix_logic_1 (
    .A(A), .B(multiplexer_1_out), .C_in(Resta), .S(SumResta), .C_out(C_out), .C2_Out(C2), .C3_out(C3));
endmodule

module ORR (
  input  [3:0] A,
  input  [3:0] B,
  output [3:0] out_3
);

  or or_1 (out_3[0], A[0], B[0]);
  or or_2 (out_3[1], A[1], B[1]);
  or or_3 (out_3[2], A[2], B[2]);
  or or_4 (out_3[3], A[3], B[3]);
endmodule

module ANDD (
  input  [3:0] A,
  input  [3:0] B,
  output [3:0] out_3
);

  and and_1 (out_3[0], A[0], B[0]);
  and and_2 (out_3[1], A[1], B[1]);
  and and_3 (out_3[2], A[2], B[2]);
  and and_4 (out_3[3], A[3], B[3]);
endmodule

module ALU (
  input  [3:0] A,
  input  [3:0] B,
  input  [1:0] OP,
  input  [1:0] OP_S,
  input  [1:0] SHIFT_R,
  input  [1:0] SHIFT_L,
  output [3:0] Resultado,
  output [3:0] A_Shift,
  output Cero,
  output Negativo,
  output C_out,
  output Overflow
);

  wire and_1_out, and_2_out, C_out_2, flags_1_overflow, not_1_out, not_2_out, not_3_out, or_1_out, or_2_out;
  wire [3:0] Result_AND, Result_OR, shiftleft_1_out_3, shiftright_1_out_3, SUMERST;

  ShiftRight shiftright_1 (.SHIFTRIGHT(SHIFT_R), .A(A), .out_3(shiftright_1_out_3));
  ShiftLeft shiftleft_1 (.SHIFT_LEFT(SHIFT_L), .A(A), .out_3(shiftleft_1_out_3));
  Multiplexer #(.select(2), .width(4)) multiplexer_1 (
    .in0(A), .in1(shiftright_1_out_3), .in2(shiftleft_1_out_3), .in3(A), .out(A_Shift), .sel(OP_S));
  not not_1 (not_1_out, OP[0]);
  not not_2 (not_2_out, C_out_2);
  and and_1 (and_1_out, C_out_2, not_1_out);
  and and_2 (and_2_out, not_2_out, OP[0]);
  and and_3 (Overflow, flags_1_overflow, OP[0]);
  or or_1 (or_1_out, and_1_out, and_2_out);
  or or_2 (or_2_out, or_1_out, flags_1_overflow);
  and and_4 (C_out, or_2_out, not_3_out);
  not not_3 (not_3_out, OP[1]);
  SumRest sumrest_1 (.Resta(OP[0]), .A(A_Shift), .B(B), .SumResta(SUMERST));  // open: C_out, C2, C3
  ORR orr_1 (.A(A_Shift), .B(B), .out_3(Result_OR));
  ANDD andd_1 (.A(A_Shift), .B(B), .out_3(Result_AND));
  Flags flags_1 (
    .RESTA(OP[0]), .A(A_Shift), .B(B), .OP1(OP[1]), .Cero(Cero), .Negativo(Negativo), .C_out(C_out_2),
    .Overflow(flags_1_overflow));
  Multiplexer #(.select(2), .width(4)) multiplexer_2 (
    .in0(SUMERST), .in1(SUMERST), .in2(Result_OR), .in3(Result_AND), .out(Resultado), .sel(OP));

  // Other names for the same wires on the sheet: OP_SHIFT[1:0] = OP_S; OP_t[1:0] = OP; Resta = OP[0]
endmodule

module Flags (
  input  RESTA,
  input  [3:0] A,
  input  [3:0] B,
  input  OP1,
  output Cero,
  output Negativo,
  output C_out,
  output Overflow
);

  wire and_1_out, not_1_out, not_2_out, not_3_out, or_1_out, or_2_out, or_3_out, sumrest_1_c2, sumrest_1_c3;
  wire [3:0] SUM_REST;

  or or_1 (or_1_out, SUM_REST[0], SUM_REST[1]);
  or or_2 (or_2_out, SUM_REST[2], SUM_REST[3]);
  or or_3 (or_3_out, or_1_out, or_2_out);
  SumRest sumrest_1 (
    .Resta(RESTA), .A(A), .B(B), .SumResta(SUM_REST), .C_out(C_out), .C2(sumrest_1_c2), .C3(sumrest_1_c3));
  and and_1 (and_1_out, SUM_REST[3], RESTA);
  not not_1 (not_1_out, or_3_out);
  not not_2 (not_2_out, OP1);
  not not_3 (not_3_out, OP1);
  and and_2 (Cero, not_1_out, not_2_out);
  and and_3 (Negativo, and_1_out, not_3_out);
  xor xor_1 (Overflow, sumrest_1_c2, sumrest_1_c3);
endmodule

module ALU4 (
  input  [3:0] A,
  input  [3:0] B,
  input  [1:0] OP,
  output [3:0] Resultado,
  output Cero,
  output Negativo,
  output C_out,
  output Overflow
);

  wire and_1_out, and_2_out, C_out_2, flags_1_overflow, not_1_out, not_2_out, not_3_out, or_1_out, or_2_out;
  wire [3:0] Result_AND, Result_OR, SUMERST;

  not not_1 (not_1_out, OP[0]);
  not not_2 (not_2_out, C_out_2);
  and and_1 (and_1_out, C_out_2, not_1_out);
  and and_2 (and_2_out, not_2_out, OP[0]);
  and and_3 (Overflow, flags_1_overflow, OP[0]);
  or or_1 (or_1_out, and_1_out, and_2_out);
  or or_2 (or_2_out, or_1_out, flags_1_overflow);
  and and_4 (C_out, or_2_out, not_3_out);
  not not_3 (not_3_out, OP[1]);
  SumRest sumrest_1 (.Resta(OP[0]), .A(A), .B(B), .SumResta(SUMERST));  // open: C_out, C2, C3
  ORR orr_1 (.A(A), .B(B), .out_3(Result_OR));
  ANDD andd_1 (.A(A), .B(B), .out_3(Result_AND));
  Flags flags_1 (
    .RESTA(OP[0]), .A(A), .B(B), .OP1(OP[1]), .Cero(Cero), .Negativo(Negativo), .C_out(C_out_2),
    .Overflow(flags_1_overflow));
  Multiplexer #(.select(2), .width(4)) multiplexer_1 (
    .in0(SUMERST), .in1(SUMERST), .in2(Result_OR), .in3(Result_AND), .out(Resultado), .sel(OP));

  // Other names for the same wires on the sheet: OP_t[1:0] = OP; Resta = OP[0]
endmodule

module ALU4_Final (
  input  [3:0] A,
  input  [3:0] B,
  input  [1:0] OP,
  output [3:0] out_4
);

  wire alu4_1_c_out, alu4_1_cero, alu4_1_negativo, alu4_1_overflow;

  ALU4 alu4_1 (
    .A(A), .B(B), .OP(OP), .Resultado(out_4), .Cero(alu4_1_cero), .Negativo(alu4_1_negativo),
    .C_out(alu4_1_c_out), .Overflow(alu4_1_overflow));
  LED led_1 (.in(alu4_1_cero));
  LED led_2 (.in(alu4_1_negativo));
  LED led_3 (.in(alu4_1_c_out));
  LED led_4 (.in(alu4_1_overflow));
endmodule
